// Logisim project alu.circ as structural Verilog: 1 circuit, main circuit alu
module alu (
  input  [31:0] A,
  input  [31:0] B,
  input  [3:0] ALUSel,
  output [31:0] Result
);

  wire comparator_1_lt, xor_2_out;
  wire [4:0] bit_extender_1_out, bit_extender_2_out, bit_extender_3_out;
  wire [31:0] add, and1, bsel, divu1, mulh1, mulhu1, mult1, multiplexer_1_out, multiplexer_2_out,
       multiplier_2_cout, negator_1_out, negator_2_out, negator_3_out, or1, remu1, sll1, slt1, sra1, srl1,
       sub, subtractor_2_out, vaddh, xor1;

  Bit_Extender #(.in_width(32), .out_width(5)) bit_extender_1 (.in(B), .out(bit_extender_1_out));
  Bit_Extender #(.in_width(32), .out_width(5)) bit_extender_2 (.in(B), .out(bit_extender_2_out));
  Bit_Extender #(.in_width(32), .out_width(5)) bit_extender_3 (.in(B), .out(bit_extender_3_out));
  Adder #(.width(32)) adder_1 (.a(A), .b(B), .out(add));  // open: cin, cout
  assign and1 = A & B;  // AND_Gate and_1, 32 bits wide
  assign or1 = A | B;  // OR_Gate or_1, 32 bits wide
  assign xor1 = A ^ B;  // XOR_Gate xor_1, 32 bits wide
  Shifter #(.width(32), .shift("lr")) shifter_1 (.in(A), .\dist (bit_extender_1_out), .out(srl1));
  Shifter #(.width(32), .shift("ar")) shifter_2 (.in(A), .\dist (bit_extender_2_out), .out(sra1));
  Shifter #(.width(32)) shifter_3 (.in(A), .\dist (bit_extender_3_out), .out(sll1));
  Comparator #(.width(32)) comparator_1 (.a(A), .b(B), .lt(comparator_1_lt));  // open: gt, eq
  Divider #(.width(32)) divider_1 (.a(A), .b(B), .out(divu1), .rem(remu1));  // open: upper
  assign slt1 = {{31{1'b0}}, comparator_1_lt};  // Bit_Extender bit_extender_4
  Multiplier #(.width(32)) multiplier_1 (.a(A), .b(B), .out(mult1), .cout(mulhu1));  // open: cin
  Negator #(.width(32)) negator_1 (.in(A), .out(negator_1_out));
  Negator #(.width(32)) negator_2 (.in(B), .out(negator_2_out));
  Multiplexer #(.width(32), .enable("false")) multiplexer_1 (
    .in0(A), .in1(negator_1_out), .out(multiplexer_1_out), .sel(A[31]));
  Multiplexer #(.width(32), .enable("false")) multiplexer_2 (
    .in0(B), .in1(negator_2_out), .out(multiplexer_2_out), .sel(B[31]));
  Subtractor #(.width(32)) subtractor_1 (.a(A), .b(B), .out(sub));  // open: bin, bout
  Multiplexer #(.width(32), .enable("false")) multiplexer_3 (.in0(A), .in1(B), .out(bsel), .sel(1'b1));
  Adder #(.width(16)) adder_2 (.a(A[15:0]), .b(B[15:0]), .out(vaddh[15:0]));  // open: cin, cout
  Adder #(.width(16)) adder_3 (.a(A[31:16]), .b(B[31:16]), .out(vaddh[31:16]));  // open: cin, cout
  Multiplier #(.width(32)) multiplier_2 (
    .a(multiplexer_1_out), .b(multiplexer_2_out), .cout(multiplier_2_cout));  // open: out, cin
  Negator #(.width(32)) negator_3 (.in(multiplier_2_cout), .out(negator_3_out));
  Subtractor #(.width(32)) subtractor_2 (.a(negator_3_out), .b(32'h1), .out(subtractor_2_out));  // open: bin, bout
  xor xor_2 (xor_2_out, A[31], B[31]);
  Multiplexer #(.width(32), .enable("false")) multiplexer_4 (
    .in0(multiplier_2_cout), .in1(subtractor_2_out), .out(mulh1), .sel(xor_2_out));
  Multiplexer #(.select(4), .width(32), .enable("false")) multiplexer_5 (
    .in0(add), .in1(and1), .in2(or1), .in3(xor1), .in4(srl1), .in5(sra1), .in6(sll1), .in7(slt1),
    .in8(divu1), .in9(remu1), .in10(mult1), .in11(mulhu1), .in12(sub), .in13(bsel), .in14(mulh1),
    .in15(vaddh), .out(Result), .sel(ALUSel));

  // Other names for the same wires on the sheet: A1 = A[31]; B1 = B[31]

  // Notes on the sheet:
  //   INPUTS to your circuit
  //   DON'T CHANGE THE LOCATIONS OF THE INPUTS AND OUTPUTS!
  //   OUTPUT from your circuit
endmodule
