// Logisim project cpu.circ as structural Verilog: 16 circuits, main circuit main
module main (
  input  [31:0] INSTRUCTION,
  input  CLOCK,
  output [31:0] FETCH_ADDRESS,
  output [31:0] ra,
  output [31:0] sp,
  output [31:0] t0,
  output [31:0] t1,
  output [31:0] t2,
  output [31:0] s0,
  output [31:0] s1,
  output [31:0] a0
);

  wire ASel, BrEq, BrLt, BrUn, BSel, DMEM_p1, DMEM_p7, DMEM_p9, DMEM_p12, DMEM_p14, DMEM_p16, JALRCheck,
       MemRW, P_PCSel, PCSel, RegWEn;
  wire [1:0] LCheck, WBSel;
  wire [3:0] ALUSel;
  wire [4:0] ImmSel;
  wire [11:0] and_1_out, Shift;
  wire [31:0] A, ALUOut, B, bit_extender_1_out, bit_extender_2_out, Data, FETCH_ADDR_WORD, Imm,
       multiplexer_1_out, multiplexer_3_out, multiplier_1_out, P_ADDR, P_INSTRUCTION, P_PCplus4, PCplus4, R1,
       R2, ReadData, register_1_q, shifter_2_out, shifter_3_out, shifter_4_out, wb;

  Multiplier #(.width(32)) multiplier_1 (.a(ALUOut), .b(32'h4), .out(multiplier_1_out));  // open: cin, cout
  Adder #(.width(32)) adder_1 (.a(FETCH_ADDRESS), .b(32'h4), .out(PCplus4));  // open: cin, cout
  Multiplexer #(.width(32), .enable("false")) multiplexer_1 (
    .in0(PCplus4), .in1(multiplier_1_out), .out(multiplexer_1_out), .sel(PCSel));
  Shifter #(.width(32), .shift("lr")) shifter_1 (.in(FETCH_ADDRESS), .\dist (5'b00010), .out(FETCH_ADDR_WORD));
  ImmGen immgen_1 (.in_1(P_INSTRUCTION[31:7]), .in_2(ImmSel), .out_3(Imm));
  Register #(.width(32)) register_1 (.D(INSTRUCTION), .clk(CLOCK), .Q(register_1_q));  // open: en, clr
  Register #(.width(32)) PC (.D(multiplexer_1_out), .clk(CLOCK), .Q(FETCH_ADDRESS));  // open: en, clr
  Multiplexer #(.width(32), .enable("false")) multiplexer_2 (
    .in0(register_1_q), .in1(32'h13), .out(P_INSTRUCTION), .sel(P_PCSel));
  LOADCheck loadcheck_1 (.Instruction(P_INSTRUCTION), .out_2(LCheck));
  ControlLogic controllogic_1 (
    .Instruction(P_INSTRUCTION), .BrEq(BrEq), .BrLt(BrLt), .PCSel(PCSel), .ImmSel(ImmSel), .BrUn(BrUn),
    .ASel(ASel), .BSel(BSel), .ALUSel(ALUSel), .MemRW(MemRW), .RegWEn(RegWEn), .WBSel(WBSel),
    .JALRCheck(JALRCheck));
  Register #(.width(32)) register_2 (.D(FETCH_ADDRESS), .clk(CLOCK), .Q(P_ADDR));  // open: en, clr
  Adder #(.width(32)) adder_2 (.a(P_ADDR), .b(32'h4), .out(P_PCplus4));  // open: cin, cout
  Shifter #(.width(32), .shift("ar")) shifter_2 (.in(P_ADDR), .\dist (5'b00010), .out(shifter_2_out));
  Multiplexer #(.width(32), .enable("false")) multiplexer_3 (
    .in0(R1), .in1(shifter_2_out), .out(multiplexer_3_out), .sel(ASel));
  Multiplexer #(.width(32), .enable("false")) multiplexer_4 (.in0(R2), .in1(Imm), .out(B), .sel(BSel));
  Register #(.width(1)) register_3 (.D(PCSel), .clk(CLOCK), .Q(P_PCSel));  // open: en, clr
  Shifter #(.width(32), .shift("ar")) shifter_3 (.in(multiplexer_3_out), .\dist (5'b00010), .out(shifter_3_out));
  Multiplexer #(.width(32), .enable("false")) multiplexer_5 (
    .in0(multiplexer_3_out), .in1(shifter_3_out), .out(A), .sel(JALRCheck));
  regfile_main RegFile (
    .rs2(P_INSTRUCTION[24:20]), .rd(P_INSTRUCTION[11:7]), .Read_Data_1(R1), .Read_Data_2(R2), .ra(ra),
    .sp(sp), .t0(t0), .t1(t1), .t2(t2), .s0(s0), .s1(s1), .a0(a0), .rs1(P_INSTRUCTION[19:15]),
    .Write_Data(wb), .RegWEn(RegWEn), .clk(CLOCK));
  BranchComp branchcomp_1 (.A(R1), .B(R2), .BrUn(BrUn), .out_4(BrEq), .out_5(BrLt));
  assign and_1_out = P_INSTRUCTION[31:20] & 12'h3;  // AND_Gate and_1, 12 bits wide
  alu Arithmetic_Logic_Unit (.A(A), .B(B), .ALUSel(ALUSel), .Result(ALUOut));
  Multiplier #(.width(12)) multiplier_2 (.a(and_1_out), .b(12'h8), .out(Shift));  // open: cin, cout
  // mem_main DMEM: pin names not known; wires that end beside it: DMEM_p1, ALUOut, R2, MemRW, CLOCK, DMEM_p1, DMEM_p7, DMEM_p7, DMEM_p9, ReadData, DMEM_p9, DMEM_p12, DMEM_p12, DMEM_p14, DMEM_p14, DMEM_p16
  Shifter #(.width(32), .shift("ar")) shifter_4 (.in(ReadData), .\dist (Shift[4:0]), .out(shifter_4_out));
  Multiplexer #(.select(2), .width(32), .enable("false")) multiplexer_6 (
    .in0(P_PCplus4), .in1(ALUOut), .in2(Data), .out(wb), .sel(WBSel));  // open: in3
  assign bit_extender_1_out = {{16{shifter_4_out[15]}}, shifter_4_out[15:0]};  // Bit_Extender bit_extender_1
  assign bit_extender_2_out = {{24{shifter_4_out[7]}}, shifter_4_out[7:0]};  // Bit_Extender bit_extender_2
  Multiplexer #(.select(2), .width(32), .enable("false")) multiplexer_7 (
    .in0(ReadData), .in1(bit_extender_1_out), .in2(bit_extender_2_out), .out(Data), .sel(LCheck));  // open: in3

  // Other names for the same wires on the sheet: clk = CLOCK; FETCH_ADDR[31:0] = FETCH_ADDRESS;
  //   rd[4:0] = P_INSTRUCTION[11:7]; r1_t[4:0] = P_INSTRUCTION[19:15]; r2_t[4:0] = P_INSTRUCTION[24:20]

  // Notes on the sheet:
  //   Output
  //   Inputs/Outputs from run.circ. DO NOT MOVE THESE.
  //   Inputs
  //   PC is Byte-Addressed
  //   Inputs/Outputs from run.circ. DO NOT MOVE THESE.
endmodule

module ImmGen (
  input  [24:0] in_1,
  input  [4:0] in_2,
  output [31:0] out_3
);

  wire [12:0] bit_extender_4_out, shifter_1_out;
  wire [20:0] bit_extender_5_out, shifter_2_out;
  wire [31:0] bit_extender_1_out, bit_extender_2_out, bit_extender_3_out, bit_extender_6_out,
       bit_extender_7_out, offset_1_out_2, offset_2_out_2, offset_3_out_2, offset_4_out_2, shifter_3_out;

  assign bit_extender_1_out = {{20{in_1[24]}}, in_1[24:13]};  // Bit_Extender bit_extender_1
  assign bit_extender_2_out = {{20{in_1[24]}}, {in_1[24:18], in_1[4:0]}};  // Bit_Extender bit_extender_2
  assign bit_extender_3_out = {{12{in_1[24]}}, in_1[24:5]};  // Bit_Extender bit_extender_3
  assign bit_extender_4_out = {{1{1'b0}}, {in_1[24], in_1[0], in_1[23:18], in_1[4:1]}};  // Bit_Extender bit_extender_4
  assign bit_extender_5_out = {{1{1'b0}}, {in_1[24], in_1[12:5], in_1[13], in_1[23:14]}};  // Bit_Extender bit_extender_5
  Shifter #(.width(13)) shifter_1 (.in(bit_extender_4_out), .\dist (4'b0001), .out(shifter_1_out));
  Shifter #(.width(21)) shifter_2 (.in(bit_extender_5_out), .\dist (5'b00001), .out(shifter_2_out));
  Shifter #(.width(32)) shifter_3 (.in(bit_extender_3_out), .\dist (5'b01100), .out(shifter_3_out));
  assign bit_extender_6_out = {{19{shifter_1_out[12]}}, shifter_1_out};  // Bit_Extender bit_extender_6
  assign bit_extender_7_out = {{11{shifter_2_out[20]}}, shifter_2_out};  // Bit_Extender bit_extender_7
  Offset offset_1 (.in_1(bit_extender_1_out), .out_2(offset_1_out_2));
  Offset offset_2 (.in_1(bit_extender_2_out), .out_2(offset_2_out_2));
  Offset offset_3 (.in_1(bit_extender_6_out), .out_2(offset_3_out_2));
  Offset offset_4 (.in_1(bit_extender_7_out), .out_2(offset_4_out_2));
  Multiplexer #(.select(5), .width(32), .enable("false")) multiplexer_1 (
    .in0(offset_1_out_2), .in4(bit_extender_1_out), .in8(offset_2_out_2), .in13(shifter_3_out),
    .in24(offset_3_out_2), .in25(offset_1_out_2), .in27(offset_4_out_2), .out(out_3), .sel(in_2));  // open: in1, in2, in3, in5, in6, in7, in9, in10, in11, in12, in14, in15, in16, in17, in18, in19, in20, in21, in22, in23, in26, in28, in29, in30, in31

  // Other names for the same wires on the sheet: Inst32_7[24:0] = in_1; funct3[2:0] = in_1[7:5]; Imm[31:0] = out_3;
  //   ImmSel[4:0] = in_2
endmodule

module Offset (
  input  [31:0] in_1,
  output [31:0] out_2
);

  wire comparator_1_lt, OffsetDiv4, Sign;
  wire [31:0] adder_2_out, divider_1_rem, multiplexer_1_out, not_1_out, not_2_out, Pos, shifter_1_out,
       shifter_2_out;

  assign not_1_out = ~in_1;  // NOT_Gate not_1, 32 bits wide
  Adder #(.width(32)) adder_1 (.a(not_1_out), .b(32'h1), .out(Pos));  // open: cin, cout
  Shifter #(.width(32), .shift("ar")) shifter_1 (.in(Pos), .\dist (5'b00010), .out(shifter_1_out));
  assign not_2_out = ~shifter_1_out;  // NOT_Gate not_2, 32 bits wide
  Adder #(.width(32)) adder_2 (.a(not_2_out), .b(32'h1), .out(adder_2_out));  // open: cin, cout
  Divider #(.width(32)) divider_1 (.a(Pos), .b(32'h4), .rem(divider_1_rem));  // open: out, upper
  Multiplexer #(.width(32), .enable("false")) multiplexer_1 (
    .in0(not_2_out), .in1(adder_2_out), .out(multiplexer_1_out), .sel(OffsetDiv4));
  Shifter #(.width(32), .shift("ar")) shifter_2 (.in(in_1), .\dist (5'b00010), .out(shifter_2_out));
  Comparator #(.width(32)) comparator_1 (.a(in_1), .b({32{1'b0}}), .lt(comparator_1_lt));  // open: gt, eq
  not not_3 (Sign, comparator_1_lt);
  Comparator #(.width(32)) comparator_2 (.a(divider_1_rem), .b({32{1'b0}}), .eq(OffsetDiv4));  // open: gt, lt
  Multiplexer #(.width(32), .enable("false")) multiplexer_2 (
    .in0(multiplexer_1_out), .in1(shifter_2_out), .out(out_2), .sel(Sign));

  // Other names for the same wires on the sheet: Offset[31:0] = in_1
endmodule

module BranchComp (
  input  [31:0] A,
  input  [31:0] B,
  input  BrUn,
  output out_4,
  output out_5
);

  wire BrEqSign, BrEqUn, BrLtSign, BrLtUn;

  Multiplexer #(.width(2), .enable("false")) multiplexer_1 (
    .in0({BrLtSign, BrEqSign}), .in1({BrLtUn, BrEqUn}), .out({out_5, out_4}), .sel(BrUn));
  Comparator #(.width(32)) comparator_1 (.a(A), .b(B), .eq(BrEqSign), .lt(BrLtSign));  // open: gt
  Comparator #(.width(32), .mode("unsigned")) comparator_2 (.a(A), .b(B), .eq(BrEqUn), .lt(BrLtUn));  // open: gt
endmodule

module ALUSelect (
  input  [31:0] in_1,
  output [3:0] out_2
);

  wire and_2_out, and_10_out, and_13_out, and_15_out, and_16_out, and_17_out, and_19_out, comparator_1_eq,
       comparator_2_eq, comparator_3_eq, comparator_4_eq, comparator_5_eq, comparator_6_eq, comparator_7_eq,
       comparator_8_eq, comparator_9_eq, comparator_10_eq, comparator_11_eq, comparator_12_eq,
       comparator_13_eq, comparator_14_eq, comparator_15_eq, comparator_16_eq, comparator_18_eq,
       comparator_19_eq, comparator_20_eq, comparator_21_eq, comparator_22_eq, comparator_23_eq,
       comparator_24_eq, comparator_25_eq, comparator_27_eq, comparator_28_eq, comparator_29_eq,
       comparator_30_eq, comparator_31_eq, comparator_32_eq, comparator_33_eq, comparator_34_eq,
       comparator_35_eq, comparator_36_eq, comparator_37_eq, eight, eleven, fifteen, five, four, fourteen,
       IorR, nine, one, or_2_out, or_3_out, seven, six, ten, thirteen, three, twelve, two;

  Comparator #(.width(7)) comparator_1 (.a(7'b0010011), .b(in_1[6:0]), .eq(comparator_1_eq));  // open: gt, lt
  Comparator #(.width(3)) comparator_2 (.a(in_1[14:12]), .b(3'b001), .eq(comparator_2_eq));  // open: gt, lt
  Comparator #(.width(3)) comparator_3 (.a(in_1[14:12]), .b(3'b010), .eq(comparator_3_eq));  // open: gt, lt
  Comparator #(.width(7)) comparator_4 (.a(7'b0110011), .b(in_1[6:0]), .eq(comparator_4_eq));  // open: gt, lt
  Comparator #(.width(7)) comparator_5 (.a(in_1[6:0]), .b(7'b0110011), .eq(comparator_5_eq));  // open: gt, lt
  Comparator #(.width(7)) comparator_6 (.a(in_1[6:0]), .b(7'b0010011), .eq(comparator_6_eq));  // open: gt, lt
  Comparator #(.width(3)) comparator_7 (.a(in_1[14:12]), .b(3'b111), .eq(comparator_7_eq));  // open: gt, lt
  Comparator #(.width(3)) comparator_8 (.a(in_1[14:12]), .b(3'b110), .eq(comparator_8_eq));  // open: gt, lt
  Comparator #(.width(3)) comparator_9 (.a(in_1[14:12]), .b(3'b100), .eq(comparator_9_eq));  // open: gt, lt
  Comparator #(.width(7)) comparator_10 (.a(in_1[31:25]), .b({7{1'b0}}), .eq(comparator_10_eq));  // open: gt, lt
  Comparator #(.width(3)) comparator_11 (.a(in_1[14:12]), .b(3'b101), .eq(comparator_11_eq));  // open: gt, lt
  Comparator #(.width(7)) comparator_12 (.a(in_1[31:25]), .b(7'b0100000), .eq(comparator_12_eq));  // open: gt, lt
  Comparator #(.width(3)) comparator_13 (.a(in_1[14:12]), .b(3'b101), .eq(comparator_13_eq));  // open: gt, lt
  Comparator #(.width(7)) comparator_14 (.a(7'b0110011), .b(in_1[6:0]), .eq(comparator_14_eq));  // open: gt, lt
  Comparator #(.width(7)) comparator_15 (.a(7'b0110011), .b(in_1[6:0]), .eq(comparator_15_eq));  // open: gt, lt
  Comparator #(.width(7)) comparator_16 (.a(in_1[6:0]), .b(7'b0010011), .eq(comparator_16_eq));  // open: gt, lt
  Comparator #(.width(7)) comparator_17 (.a(in_1[6:0]), .b(7'b0110111), .eq(thirteen));  // open: gt, lt
  Comparator #(.width(7)) comparator_18 (.a(in_1[31:25]), .b(7'b0001111), .eq(comparator_18_eq));  // open: gt, lt
  Comparator #(.width(3)) comparator_19 (.a(in_1[14:12]), .b(3'b000), .eq(comparator_19_eq));  // open: gt, lt
  or or_1 (IorR, comparator_5_eq, comparator_6_eq);
  and and_1 (one, IorR, comparator_7_eq);
  or or_2 (or_2_out, comparator_14_eq, comparator_1_eq);
  or or_3 (or_3_out, comparator_15_eq, comparator_16_eq);
  and and_2 (and_2_out, comparator_18_eq, comparator_19_eq);
  and and_3 (two, IorR, comparator_8_eq);
  and and_4 (three, IorR, comparator_9_eq);
  and and_5 (four, comparator_10_eq, comparator_11_eq);
  and and_6 (five, comparator_12_eq, comparator_13_eq);
  and and_7 (six, or_2_out, comparator_2_eq);
  and and_8 (seven, or_3_out, comparator_3_eq);
  and and_9 (fifteen, comparator_4_eq, and_2_out);
  Comparator #(.width(7)) comparator_20 (.a(in_1[31:25]), .b(7'b0000001), .eq(comparator_20_eq));  // open: gt, lt
  Comparator #(.width(3)) comparator_21 (.a(in_1[14:12]), .b(3'b101), .eq(comparator_21_eq));  // open: gt, lt
  Comparator #(.width(7)) comparator_22 (.a(7'b0110011), .b(in_1[6:0]), .eq(comparator_22_eq));  // open: gt, lt
  Comparator #(.width(7)) comparator_23 (.a(in_1[31:25]), .b(7'b0000001), .eq(comparator_23_eq));  // open: gt, lt
  Comparator #(.width(3)) comparator_24 (.a(in_1[14:12]), .b(3'b111), .eq(comparator_24_eq));  // open: gt, lt
  Comparator #(.width(7)) comparator_25 (.a(7'b0110011), .b(in_1[6:0]), .eq(comparator_25_eq));  // open: gt, lt
  Comparator #(.width(3)) comparator_26 (.a(in_1[14:12]), .b(3'b011), .eq(eleven));  // open: gt, lt
  Comparator #(.width(7)) comparator_27 (.a(7'b0110011), .b(in_1[6:0]), .eq(comparator_27_eq));  // open: gt, lt
  Comparator #(.width(3)) comparator_28 (.a(in_1[14:12]), .b(3'b011), .eq(comparator_28_eq));  // open: gt, lt
  Comparator #(.width(7)) comparator_29 (.a(7'b0110011), .b(in_1[6:0]), .eq(comparator_29_eq));  // open: gt, lt
  Comparator #(.width(7)) comparator_30 (.a(7'b0110011), .b(in_1[6:0]), .eq(comparator_30_eq));  // open: gt, lt
  and and_10 (and_10_out, comparator_23_eq, comparator_24_eq);
  Comparator #(.width(7)) comparator_31 (.a(in_1[31:25]), .b(7'b0000001), .eq(comparator_31_eq));  // open: gt, lt
  Comparator #(.width(3)) comparator_32 (.a(in_1[14:12]), .b(3'b000), .eq(comparator_32_eq));  // open: gt, lt
  Comparator #(.width(7)) comparator_33 (.a(in_1[31:25]), .b(7'b0100000), .eq(comparator_33_eq));  // open: gt, lt
  Comparator #(.width(3)) comparator_34 (.a(in_1[14:12]), .b(3'b000), .eq(comparator_34_eq));  // open: gt, lt
  Comparator #(.width(7)) comparator_35 (.a(7'b0111011), .b(in_1[6:0]), .eq(comparator_35_eq));  // open: gt, lt
  Comparator #(.width(7)) comparator_36 (.a(in_1[31:25]), .b(7'b0000001), .eq(comparator_36_eq));  // open: gt, lt
  Comparator #(.width(3)) comparator_37 (.a(in_1[14:12]), .b(3'b001), .eq(comparator_37_eq));  // open: gt, lt
  Priority_Encoder #(.select(4)) priority_encoder_1 (
    .in0(1'b1), .in1(one), .in2(two), .in3(three), .in4(four), .in5(five), .in6(six), .in7(seven),
    .in8(eight), .in9(nine), .in10(ten), .in11(eleven), .in12(twelve), .in13(thirteen), .in14(fourteen),
    .in15(fifteen), .out(out_2));  // open: gs, en_out, en_in
  and and_11 (eight, comparator_20_eq, comparator_21_eq, comparator_30_eq);
  and and_12 (nine, comparator_22_eq, and_10_out);
  and and_13 (and_13_out, comparator_31_eq, comparator_32_eq);
  and and_14 (ten, comparator_25_eq, and_13_out);
  and and_15 (and_15_out, comparator_27_eq, and_16_out);
  and and_16 (and_16_out, comparator_33_eq, comparator_34_eq);
  and and_17 (and_17_out, comparator_35_eq, comparator_28_eq);
  and and_18 (fourteen, comparator_29_eq, and_19_out);
  and and_19 (and_19_out, comparator_36_eq, comparator_37_eq);
  or or_4 (twelve, and_15_out, and_17_out);

  // Other names for the same wires on the sheet: opcode[6:0] = in_1[6:0]; funct3[2:0] = in_1[14:12];
  //   funct7[6:0] = in_1[31:25]
endmodule

module ControlLogic (
  input  [31:0] Instruction,
  input  BrEq,
  input  BrLt,
  output PCSel,
  output [4:0] ImmSel,
  output BrUn,
  output ASel,
  output BSel,
  output [3:0] ALUSel,
  output MemRW,
  output RegWEn,
  output [1:0] WBSel,
  output JALRCheck
);

  wire I_A, I_B, I_BrUn, I_J_A, I_J_B, I_J_BrUn, I_J_JALR, I_J_MemRW, I_J_PC, I_J_RegWEn, I_JALR, I_L_A,
       I_L_B, I_L_BrUn, I_L_JALR, I_L_MemRW, I_L_PC, I_L_RegWEn, I_MemRW, I_PC, I_RegWEn, R_A, R_B, R_BrUn,
       R_JALR, R_MemRW, R_PC, R_RegWEn, S_A, S_B, S_BrUn, S_JALR, S_MemRW, S_PC, S_RegWEn, SB_A, SB_B,
       SB_BrUn, SB_JALR, SB_MemRW, SB_PC, SB_RegWEn, U_A, U_B, U_BrUn, U_JALR, U_MemRW, U_PC, U_RegWEn, UJ_A,
       UJ_B, UJ_BrUn, UJ_JALR, UJ_MemRW, UJ_PC, UJ_RegWEn;
  wire [1:0] I_J_WB, I_L_WB, I_WB, R_WB, S_WB, SB_WB, U_WB, UJ_WB;
  wire [4:0] I_Imm, I_J_Imm, I_L_Imm, R_Imm, S_Imm, SB_Imm, U_Imm, UJ_Imm;

  RType rtype_1 (
    .Instruction(Instruction), .BrEq(BrEq), .BrLt(BrLt), .out_4(R_PC), .out_5(R_Imm), .out_6(R_BrUn),
    .out_7(R_A), .out_8(R_B), .out_9(R_MemRW), .out_10(R_RegWEn), .out_11(R_WB), .out_12(R_JALR));
  IType itype_1 (
    .Instruction(Instruction), .BrEq(BrEq), .BrLt(BrLt), .out_4(I_PC), .out_5(I_Imm), .out_6(I_BrUn),
    .out_7(I_A), .out_8(I_B), .out_9(I_MemRW), .out_10(I_RegWEn), .out_11(I_WB), .out_12(I_JALR));
  SType stype_1 (
    .Instruction(Instruction), .BrEq(BrEq), .BrLt(BrLt), .out_4(S_PC), .out_5(S_Imm), .out_6(S_BrUn),
    .out_7(S_A), .out_8(S_B), .out_9(S_MemRW), .out_10(S_RegWEn), .out_11(S_WB), .out_12(S_JALR));
  SBType sbtype_1 (
    .Instruction(Instruction), .BrEq(BrEq), .BrLt(BrLt), .out_4(SB_PC), .out_5(SB_Imm), .out_6(SB_BrUn),
    .out_7(SB_A), .out_8(SB_B), .out_9(SB_MemRW), .out_10(SB_RegWEn), .out_11(SB_WB), .out_12(SB_JALR));
  JALR jalr_1 (
    .Instruction(Instruction), .BrEq(BrEq), .BrLt(BrLt), .out_4(I_J_PC), .out_5(I_J_Imm), .out_6(I_J_BrUn),
    .out_7(I_J_A), .out_8(I_J_B), .out_9(I_J_MemRW), .out_10(I_J_RegWEn), .out_11(I_J_WB), .out_12(I_J_JALR));
  LOAD load_1 (
    .Instruction(Instruction), .BrEq(BrEq), .BrLt(BrLt), .out_4(I_L_PC), .out_5(I_L_Imm), .out_6(I_L_BrUn),
    .out_7(I_L_A), .out_8(I_L_B), .out_9(I_L_MemRW), .out_10(I_L_RegWEn), .out_11(I_L_WB), .out_12(I_L_JALR));
  UType utype_1 (
    .Instruction(Instruction), .BrEq(BrEq), .BrLt(BrLt), .out_4(U_PC), .out_5(U_Imm), .out_6(U_BrUn),
    .out_7(U_A), .out_8(U_B), .out_9(U_MemRW), .out_10(U_RegWEn), .out_11(U_WB), .out_12(U_JALR));
  UJType ujtype_1 (
    .Instruction(Instruction), .BrEq(BrEq), .BrLt(BrLt), .out_4(UJ_PC), .out_5(UJ_Imm), .out_6(UJ_BrUn),
    .out_7(UJ_A), .out_8(UJ_B), .out_9(UJ_MemRW), .out_10(UJ_RegWEn), .out_11(UJ_WB), .out_12(UJ_JALR));
  Multiplexer #(.select(5), .enable("false")) multiplexer_1 (
    .in0(I_L_PC), .in4(I_PC), .in8(S_PC), .in12(R_PC), .in13(U_PC), .in24(SB_PC), .in25(I_J_PC),
    .in27(UJ_PC), .out(PCSel), .sel(Instruction[6:2]));  // open: in1, in2, in3, in5, in6, in7, in9, in10, in11, in14, in15, in16, in17, in18, in19, in20, in21, in22, in23, in26, in28, in29, in30, in31
  Multiplexer #(.select(5), .enable("false")) multiplexer_2 (
    .in0(I_L_BrUn), .in4(I_BrUn), .in8(S_BrUn), .in12(R_BrUn), .in13(U_BrUn), .in24(SB_BrUn),
    .in25(I_J_BrUn), .in27(UJ_BrUn), .out(BrUn), .sel(Instruction[6:2]));  // open: in1, in2, in3, in5, in6, in7, in9, in10, in11, in14, in15, in16, in17, in18, in19, in20, in21, in22, in23, in26, in28, in29, in30, in31
  Multiplexer #(.select(5), .enable("false")) multiplexer_3 (
    .in0(I_L_B), .in4(I_B), .in8(S_B), .in12(R_B), .in13(U_B), .in24(SB_B), .in25(I_J_B), .in27(UJ_B),
    .out(BSel), .sel(Instruction[6:2]));  // open: in1, in2, in3, in5, in6, in7, in9, in10, in11, in14, in15, in16, in17, in18, in19, in20, in21, in22, in23, in26, in28, in29, in30, in31
  Multiplexer #(.select(5), .enable("false")) multiplexer_4 (
    .in0(I_L_MemRW), .in4(I_MemRW), .in8(S_MemRW), .in12(R_MemRW), .in13(U_MemRW), .in24(SB_MemRW),
    .in25(I_J_MemRW), .in27(UJ_MemRW), .out(MemRW), .sel(Instruction[6:2]));  // open: in1, in2, in3, in5, in6, in7, in9, in10, in11, in14, in15, in16, in17, in18, in19, in20, in21, in22, in23, in26, in28, in29, in30, in31
  Multiplexer #(.select(5), .width(2), .enable("false")) multiplexer_5 (
    .in0(I_L_WB), .in4(I_WB), .in8(S_WB), .in12(R_WB), .in13(U_WB), .in24(SB_WB), .in25(I_J_WB),
    .in27(UJ_WB), .out(WBSel), .sel(Instruction[6:2]));  // open: in1, in2, in3, in5, in6, in7, in9, in10, in11, in14, in15, in16, in17, in18, in19, in20, in21, in22, in23, in26, in28, in29, in30, in31
  Multiplexer #(.select(5), .width(5), .enable("false")) multiplexer_6 (
    .in0(I_L_Imm), .in4(I_Imm), .in8(S_Imm), .in12(R_Imm), .in13(U_Imm), .in24(SB_Imm), .in25(I_J_Imm),
    .in27(UJ_Imm), .out(ImmSel), .sel(Instruction[6:2]));  // open: in1, in2, in3, in5, in6, in7, in9, in10, in11, in14, in15, in16, in17, in18, in19, in20, in21, in22, in23, in26, in28, in29, in30, in31
  Multiplexer #(.select(5), .enable("false")) multiplexer_7 (
    .in0(I_L_A), .in4(I_A), .in8(S_A), .in12(R_A), .in13(U_A), .in24(SB_A), .in25(I_J_A), .in27(UJ_A),
    .out(ASel), .sel(Instruction[6:2]));  // open: in1, in2, in3, in5, in6, in7, in9, in10, in11, in14, in15, in16, in17, in18, in19, in20, in21, in22, in23, in26, in28, in29, in30, in31
  Multiplexer #(.select(5), .enable("false")) multiplexer_8 (
    .in0(I_L_JALR), .in4(I_JALR), .in8(S_JALR), .in12(R_JALR), .in13(U_JALR), .in24(SB_JALR),
    .in25(I_J_JALR), .in27(UJ_JALR), .out(JALRCheck), .sel(Instruction[6:2]));  // open: in1, in2, in3, in5, in6, in7, in9, in10, in11, in14, in15, in16, in17, in18, in19, in20, in21, in22, in23, in26, in28, in29, in30, in31
  Multiplexer #(.select(5), .enable("false")) multiplexer_9 (
    .in0(I_L_RegWEn), .in4(I_RegWEn), .in8(S_RegWEn), .in12(R_RegWEn), .in13(U_RegWEn), .in24(SB_RegWEn),
    .in25(I_J_RegWEn), .in27(UJ_RegWEn), .out(RegWEn), .sel(Instruction[6:2]));  // open: in1, in2, in3, in5, in6, in7, in9, in10, in11, in14, in15, in16, in17, in18, in19, in20, in21, in22, in23, in26, in28, in29, in30, in31
  ALUSelect aluselect_1 (.in_1(Instruction), .out_2(ALUSel));

  // Other names for the same wires on the sheet: opcode_less[4:0] = Instruction[6:2]
endmodule

module RType (
  input  [31:0] Instruction,
  input  BrEq,
  input  BrLt,
  output out_4,
  output [4:0] out_5,
  output out_6,
  output out_7,
  output out_8,
  output out_9,
  output out_10,
  output [1:0] out_11,
  output out_12
);


  assign out_4 = 1'b0;
  assign out_5 = 5'b01100;
  assign out_6 = 1'b1;
  assign out_7 = 1'b0;
  assign out_8 = 1'b0;
  assign out_9 = 1'b0;
  assign out_10 = 1'b1;
  assign out_11 = 2'b01;
  assign out_12 = 1'b0;
endmodule

module IType (
  input  [31:0] Instruction,
  input  BrEq,
  input  BrLt,
  output out_4,
  output [4:0] out_5,
  output out_6,
  output out_7,
  output out_8,
  output out_9,
  output out_10,
  output [1:0] out_11,
  output out_12
);


  assign out_4 = 1'b0;
  assign out_5 = 5'b00100;
  assign out_6 = 1'b1;
  assign out_7 = 1'b0;
  assign out_8 = 1'b1;
  assign out_9 = 1'b0;
  assign out_10 = 1'b1;
  assign out_11 = 2'b01;
  assign out_12 = 1'b0;
endmodule

module SType (
  input  [31:0] Instruction,
  input  BrEq,
  input  BrLt,
  output out_4,
  output [4:0] out_5,
  output out_6,
  output out_7,
  output out_8,
  output out_9,
  output out_10,
  output [1:0] out_11,
  output out_12
);


  assign out_4 = 1'b0;
  assign out_5 = 5'b01000;
  assign out_6 = 1'b1;
  assign out_7 = 1'b0;
  assign out_8 = 1'b1;
  assign out_9 = 1'b1;
  assign out_10 = 1'b0;
  assign out_11 = 2'b01;
  assign out_12 = 1'b0;
endmodule

module SBType (
  input  [31:0] Instruction,
  input  BrEq,
  input  BrLt,
  output out_4,
  output [4:0] out_5,
  output out_6,
  output out_7,
  output out_8,
  output out_9,
  output out_10,
  output [1:0] out_11,
  output out_12
);

  wire not_1_out;

  Comparator #(.width(3)) comparator_1 (.a(Instruction[14:12]), .b(3'b110), .eq(out_6));  // open: gt, lt
  not not_1 (not_1_out, BrEq);
  Multiplexer #(.select(3), .enable("false")) multiplexer_1 (
    .in0(BrEq), .in1(not_1_out), .in4(BrLt), .in6(BrLt), .out(out_4), .sel(Instruction[14:12]));  // open: in2, in3, in5, in7

  assign out_5 = 5'b11000;
  assign out_7 = 1'b1;
  assign out_8 = 1'b1;
  assign out_9 = 1'b0;
  assign out_10 = 1'b0;
  assign out_11 = 2'b01;
  assign out_12 = 1'b0;

  // Other names for the same wires on the sheet: BrUn = out_6; funct3[2:0] = Instruction[14:12];
  //   imm[11:0] = Instruction[31:20]; PCSel = out_4
endmodule

module UType (
  input  [31:0] Instruction,
  input  BrEq,
  input  BrLt,
  output out_4,
  output [4:0] out_5,
  output out_6,
  output out_7,
  output out_8,
  output out_9,
  output out_10,
  output [1:0] out_11,
  output out_12
);


  assign out_4 = 1'b0;
  assign out_5 = 5'b01101;
  assign out_6 = 1'b1;
  assign out_7 = 1'b0;
  assign out_8 = 1'b1;
  assign out_9 = 1'b0;
  assign out_10 = 1'b1;
  assign out_11 = 2'b01;
  assign out_12 = 1'b0;
endmodule

module UJType (
  input  [31:0] Instruction,
  input  BrEq,
  input  BrLt,
  output out_4,
  output [4:0] out_5,
  output out_6,
  output out_7,
  output out_8,
  output out_9,
  output out_10,
  output [1:0] out_11,
  output out_12
);


  assign out_4 = 1'b1;
  assign out_5 = 5'b11011;
  assign out_6 = 1'b1;
  assign out_7 = 1'b1;
  assign out_8 = 1'b1;
  assign out_9 = 1'b0;
  assign out_10 = 1'b1;
  assign out_11 = 2'b00;
  assign out_12 = 1'b0;
endmodule

module JALR (
  input  [31:0] Instruction,
  input  BrEq,
  input  BrLt,
  output out_4,
  output [4:0] out_5,
  output out_6,
  output out_7,
  output out_8,
  output out_9,
  output out_10,
  output [1:0] out_11,
  output out_12
);


  assign out_4 = 1'b1;
  assign out_5 = 5'b00100;
  assign out_6 = 1'b1;
  assign out_7 = 1'b0;
  assign out_8 = 1'b1;
  assign out_9 = 1'b0;
  assign out_10 = 1'b1;
  assign out_11 = 2'b00;
  assign out_12 = 1'b1;
endmodule

module LOAD (
  input  [31:0] Instruction,
  input  BrEq,
  input  BrLt,
  output out_4,
  output [4:0] out_5,
  output out_6,
  output out_7,
  output out_8,
  output out_9,
  output out_10,
  output [1:0] out_11,
  output out_12
);


  assign out_4 = 1'b0;
  assign out_5 = {5{1'b0}};
  assign out_6 = 1'b1;
  assign out_7 = 1'b0;
  assign out_8 = 1'b1;
  assign out_9 = 1'b0;
  assign out_10 = 1'b1;
  assign out_11 = 2'b10;
  assign out_12 = 1'b0;
endmodule

module JALRCheck (
  input  [31:0] Instruction,
  output out_2
);

  Multiplexer #(.select(5), .enable("false")) multiplexer_1 (
    .in0(1'b0), .in4(1'b0), .in8(1'b0), .in12(1'b0), .in13(1'b0), .in24(1'b0), .in25(1'b1), .in27(1'b0),
    .out(out_2), .sel(Instruction[6:2]));  // open: in1, in2, in3, in5, in6, in7, in9, in10, in11, in14, in15, in16, in17, in18, in19, in20, in21, in22, in23, in26, in28, in29, in30, in31

  // Other names for the same wires on the sheet: opcode_less[4:0] = Instruction[6:2]; JALRCheck = out_2
endmodule

module LOADCheck (
  input  [31:0] Instruction,
  output [1:0] out_2
);

  wire [1:0] multiplexer_1_out;

  Multiplexer #(.select(3), .width(2), .enable("false")) multiplexer_1 (
    .in0(2'b10), .in1(2'b01), .in2(2'b00), .out(multiplexer_1_out), .sel(Instruction[14:12]));  // open: in3, in4, in5, in6, in7
  Multiplexer #(.select(5), .width(2), .enable("false")) multiplexer_2 (
    .in0(multiplexer_1_out), .in4(2'b00), .in8(2'b00), .in12(2'b00), .in13(2'b00), .in24(2'b00),
    .in25(2'b00), .in27(2'b00), .out(out_2), .sel(Instruction[6:2]));  // open: in1, in2, in3, in5, in6, in7, in9, in10, in11, in14, in15, in16, in17, in18, in19, in20, in21, in22, in23, in26, in28, in29, in30, in31

  // Other names for the same wires on the sheet: opcode_less[4:0] = Instruction[6:2];
  //   funct3[2:0] = Instruction[14:12]; LoadCheck[1:0] = out_2
endmodule
